# Fritzing sketch Micro-MemorySequence (saved by Fritzing 1.0.6)
breadboards: 1
perfboards: 1

parts:
  S1 = Momentary Switch 6mm 2pin
  S2 = Momentary Switch 6mm 2pin
  S3 = Momentary Switch 6mm 2pin
  S4 = Momentary Switch 6mm 2pin
  BAT1 = Battery Holders [package=battcom_20mm_pth]  # not connected
  JP1 = Header 1 [package=1x01_offset]
  JP2 = Header 1 [package=1x01_offset]  # not connected
  JP3 = Header 1 [package=1x01_offset]  # not connected
  JP4 = Header 1 [package=1x01_offset]  # not connected
  JP5 = Header 1 [package=1x01_offset]  # not connected
  JP6 = Header 1 [package=1x01_offset]  # not connected
  JP7 = Header 1 [package=1x01_offset]  # not connected
  JP8 = Header 1 [package=1x01_offset]  # not connected
  JP9 = Header 1 [package=1x01_offset]
  U1 = ATTINY13 [package=dip]
  U2 = DIP - 8 pins socket [package="DIP (Dual Inline) [THT]"]
  buz1 = Piezo Buzzer

nets:
  N1: S1.1, S2.1, S3.1, S4.1, JP9.1, U1.GND, U2.pin4, buz1.pin_2
  N2: S4.2, U2.pin3
  N3: JP1.1, U1.VCC, U2.pin8
  N4: U1.PB5(NRES), U2.pin1
  N5: U1.PB0(MOSI), U2.pin5
  N6: U2.pin7, buz1.pin_1

notes:
  ユニバーサル基板
  タクトスイッチ #1
  タクトスイッチ #2
  タクトスイッチ #3
  タクトスイッチ #4
  ピンヘッダ 9P
  コイン電池ホルダー
  パッシブブザー
  DIP8 IC ソケット
  ATtiny13A
  ミニブレッドボード

custom parts:
  Momentary Switch 6mm 2pin: Momentary Switch 6mm 2 pin Button commonly used for reset or general input.
  DIP - 8 pins socket: A DIP socket. With 8 pins on a 300mil dual inline package (DIP) footprint.
  Piezo Buzzer: Part from https://www.nutsvolts.com/magazine/article/november2012_SmileysWorkshop. Breadboard and icon images modified to be 0.3" in spacing and be more similar to the actual physical part.
